# Fritzing sketch uncloud (saved by Fritzing 0.9.0b)
breadboards: 1

parts:
  Power_to_NUC(-) = Screw terminal - 2 pins [package=THT]
  Ampmeter_out_to_NUC(+) = Screw terminal - 2 pins [package=THT]
  Battery(-) = Screw terminal - 2 pins [package=THT]
  Battery(+) = Screw terminal - 2 pins [package=THT]
  SLA_Battery = DC Power [voltage=12V]
  Fuse = Fuse with Handler [part_number=Htc-15m]
  Ampmeter_in(+) = screw terminal, 2 pins
  Yocto-Amp = Amperemeter
  Yocto-Volt = Voltmeter
  CONN1 = USB connector [package=THT]
  CONN2 = USB connector [package=THT]
  CONN3 = USB connector [package=THT]
  CONN4 = USB connector [package=THT]
  Power_plug1 = Power plug

nets:
  N1: Power_to_NUC(-).pin1, Power_plug1.GND
  N2: Power_to_NUC(-).pin2, Battery(-).pin1, Yocto-Volt.Positive
  N3: Ampmeter_out_to_NUC(+).pin1, Power_plug1.VCC
  N4: Ampmeter_out_to_NUC(+).pin2, Yocto-Amp.Positive
  N5: Battery(-).pin2, Fuse.Connector1
  N6: Battery(+).pin1, Ampmeter_in(+).pin2, Yocto-Volt.Com
  N7: Battery(+).pin2, SLA_Battery.V+
  N8: SLA_Battery.V-, Fuse.Connector2
  N9: Ampmeter_in(+).pin1, Yocto-Amp.Com
  5V: CONN1.5V, CONN4.5V
  N10: CONN1.d-, CONN4.d-
  N11: CONN1.d+, CONN4.d+
  GND: CONN1.GND, CONN1.chassis5, CONN4.GND, CONN4.chassis6
  5V_2: CONN2.5V, CONN3.5V
  N12: CONN2.d-, CONN3.d-
  N13: CONN2.d+, CONN3.d+
  GND_2: CONN2.GND, CONN3.GND, CONN3.chassis5

notes:
  NUC
  UNCloud, Providing computing services without a consistent power or world wide web connection, 1.3

custom parts:
  Amperemeter: A Standard Multimeter in Current mode
  Voltmeter: A Standard Multimeter in Current mode
